# Fritzing sketch elektricna_shema (saved by Fritzing 0.9.3b)
breadboards: 1

parts:
  Rele_2 = Relay [part_number=FRS1B-S package=THT]
  Rele_1 = Relay [part_number=FRS1B-S package=THT]
  S1 = SWITCH-MOMENTARY-2 [package=tactile-switch-1101ne]
  S2 = SWITCH-MOMENTARY-2 [package=tactile-switch-1101ne]
  S3 = SWITCH-MOMENTARY-2 [package=tactile-switch-1101ne]
  Part1 = Arduino Uno (Rev3)
  Rele_3 = Relay [part_number=FRS1B-S package=THT]
  MPX4250AP1 = MPX4250AP pressure sensor [part_number=MPX]

nets:
  N1: Rele_2.COIL1, Rele_1.COIL2, Part1.5V, Rele_3.COIL1, MPX4250AP1.Vs
  N2: Rele_2.C1, Rele_2.C2, Part1.D9_PWM
  GND: Rele_2.COIL2, Rele_1.COIL1, S1.1, Part1.GND, Rele_3.COIL2, MPX4250AP1.GND
  N3: Rele_1.C1, Rele_1.C2, Part1.D7
  N4: S1.2, Part1.A2
  N5: S2.2, Part1.A1
  N6: S3.2, Part1.A0
  N7: Part1.A3, MPX4250AP1.V_out
  N8: Part1.A4/SDA, Part1.A5/SCL
  N9: Part1.D8, Rele_3.C1
  N10: Part1.D10_PWM/SS, Part1.D11_PWM/MOSI, Part1.D12/MISO, Part1.D13/SCK
  N11: Part1.D5_PWM, Part1.D6_PWM

notes:
  Driver 10,11,12,13
  Screen outputs SDA, SCL, 5, 6
